# Fritzing sketch firePIR (saved by Fritzing 0.9.3b)
breadboards: 1

parts:
  Part1 = Arduino Uno (Rev3)
  R1 = Photocell (LDR) [package=THT]
  R2 = Resistor [tolerance=±5% resistance=18k package=THT]
  RGB_SMD_LED1 = SMD RGB LED (WS2812) [package=5050]
  LED1 = LED - 5mm [color="Red (633nm)" package="5 mm [THT]"]
  R3 = Resistor [tolerance=±5% resistance=150 package=THT]
  R4 = Resistor [tolerance=±5% resistance=220 package=THT]
  C1 = Electrolytic Capacitor [capacitance=100µF voltage=35V package="100 mil [THT, electrolytic]"]  # not connected

nets:
  N1: Part1.A0, R1.pin_1, R2.Pin_0
  N2: Part1.D13/SCK, R3.Pin_0
  N3: Part1.D6_PWM, R4.Pin_0
  5V: Part1.5V, R2.Pin_1, RGB_SMD_LED1.VDD
  GND: Part1.GND, R1.pin_0, RGB_SMD_LED1.VSS, LED1.anode
  N4: RGB_SMD_LED1.NC, R4.Pin_1
  N5: LED1.cathode, R3.Pin_1
